// Logisim project micro.circ as structural Verilog: 1 circuit, main circuit EV20_Superescalar
module EV20_Superescalar (
  input  in_1
);

  wire ALU_is_done, ALU_is_free, ALUALULAU_cyout, and_1_out, and_2_out, and_3_out, and_4_out, and_5_out,
       and_6_out, and_7_out, and_8_out, and_9_out, and_10_out, bloque1_bsr_1_p6, CLK, CLK2, CLK3, CLK4, CYin,
       HOLD, jumpcont_1_p4, LatchMemEnable, MEM_is_done, mem_is_free, nor_1_out, not_1_out, not_2_out,
       not_3_out, not_4_out, not_5_out, not_6_out, not_7_out, not_8_out, or_1_out, or_2_out, or_3_out,
       or_4_out, or_5_out, or_6_out, or_7_out, or_8_out, pipeline_register_viewer_1_a_is_enabled,
       pipeline_register_viewer_1_b_is_enabled, pipeline_register_viewer_1_c_is_enabled,
       pipeline_register_viewer_2_a_is_enabled, pipeline_register_viewer_2_b_is_enabled,
       pipeline_register_viewer_2_c_is_enabled, pipeline_register_viewer_3_a_is_enabled,
       pipeline_register_viewer_3_b_is_enabled, pipeline_register_viewer_3_c_is_enabled,
       pipeline_register_viewer_4_a_is_enabled, pipeline_register_viewer_4_b_is_enabled,
       pipeline_register_viewer_4_c_is_enabled, Pr, preloadenablee, register_2_q, register_3_q,
       register_bank_viewer_1_a_is_enabled, register_bank_viewer_1_b_is_enabled,
       register_bank_viewer_1_c_is_enabled, T, tvvv, uc1_1_p5, uc1_1_p6, UC1_HOLD, undriven, undriven_2,
       undriven_3, undriven_5, undriven_6, undriven_7;
  wire [1:0] ALU_Pipeline_sh_out, MREtapa2Pipeline, MRMW, pipeline_register_1_mrymw_out,
       pipeline_register_1_sh_out, undriven_4;
  wire [2:0] bloque1_bsr_1_p4_2;
  wire [3:0] ALU_Pipeline_aluc_out, pipeline_register_1_aluc_out, pipeline_register_viewer_1_a_lsn,
       pipeline_register_viewer_1_a_msn, pipeline_register_viewer_1_b0, pipeline_register_viewer_1_b1,
       pipeline_register_viewer_1_b2, pipeline_register_viewer_1_b3, pipeline_register_viewer_1_b4,
       pipeline_register_viewer_1_b5, pipeline_register_viewer_1_b6, pipeline_register_viewer_1_b7,
       pipeline_register_viewer_1_b8, pipeline_register_viewer_1_b9, pipeline_register_viewer_1_b10,
       pipeline_register_viewer_1_b11, pipeline_register_viewer_1_b12, pipeline_register_viewer_1_b13,
       pipeline_register_viewer_1_b14, pipeline_register_viewer_1_b15, pipeline_register_viewer_1_b16,
       pipeline_register_viewer_1_b_lsn, pipeline_register_viewer_1_b_msn, pipeline_register_viewer_1_c_lsn,
       pipeline_register_viewer_1_c_msn, pipeline_register_viewer_2_a_lsn, pipeline_register_viewer_2_a_msn,
       pipeline_register_viewer_2_b0, pipeline_register_viewer_2_b1, pipeline_register_viewer_2_b2,
       pipeline_register_viewer_2_b3, pipeline_register_viewer_2_b4, pipeline_register_viewer_2_b5,
       pipeline_register_viewer_2_b6, pipeline_register_viewer_2_b7, pipeline_register_viewer_2_b8,
       pipeline_register_viewer_2_b9, pipeline_register_viewer_2_b10, pipeline_register_viewer_2_b11,
       pipeline_register_viewer_2_b12, pipeline_register_viewer_2_b13, pipeline_register_viewer_2_b14,
       pipeline_register_viewer_2_b15, pipeline_register_viewer_2_b16, pipeline_register_viewer_2_b_lsn,
       pipeline_register_viewer_2_b_msn, pipeline_register_viewer_2_c_lsn, pipeline_register_viewer_2_c_msn,
       pipeline_register_viewer_3_a_lsn, pipeline_register_viewer_3_a_msn, pipeline_register_viewer_3_b0,
       pipeline_register_viewer_3_b1, pipeline_register_viewer_3_b2, pipeline_register_viewer_3_b3,
       pipeline_register_viewer_3_b4, pipeline_register_viewer_3_b5, pipeline_register_viewer_3_b6,
       pipeline_register_viewer_3_b7, pipeline_register_viewer_3_b8, pipeline_register_viewer_3_b9,
       pipeline_register_viewer_3_b10, pipeline_register_viewer_3_b11, pipeline_register_viewer_3_b12,
       pipeline_register_viewer_3_b13, pipeline_register_viewer_3_b14, pipeline_register_viewer_3_b15,
       pipeline_register_viewer_3_b16, pipeline_register_viewer_3_b_lsn, pipeline_register_viewer_3_b_msn,
       pipeline_register_viewer_3_c_lsn, pipeline_register_viewer_3_c_msn, pipeline_register_viewer_4_a_lsn,
       pipeline_register_viewer_4_a_msn, pipeline_register_viewer_4_b0, pipeline_register_viewer_4_b1,
       pipeline_register_viewer_4_b2, pipeline_register_viewer_4_b3, pipeline_register_viewer_4_b4,
       pipeline_register_viewer_4_b5, pipeline_register_viewer_4_b6, pipeline_register_viewer_4_b7,
       pipeline_register_viewer_4_b8, pipeline_register_viewer_4_b9, pipeline_register_viewer_4_b10,
       pipeline_register_viewer_4_b11, pipeline_register_viewer_4_b12, pipeline_register_viewer_4_b13,
       pipeline_register_viewer_4_b14, pipeline_register_viewer_4_b15, pipeline_register_viewer_4_b16,
       pipeline_register_viewer_4_b_lsn, pipeline_register_viewer_4_b_msn, pipeline_register_viewer_4_c_lsn,
       pipeline_register_viewer_4_c_msn, register_bank_viewer_1_a_address_n0,
       register_bank_viewer_1_a_address_n1, register_bank_viewer_1_a_address_n2,
       register_bank_viewer_1_a_address_n3, register_bank_viewer_1_a_data_lsn,
       register_bank_viewer_1_a_data_msn, register_bank_viewer_1_b_address_n0,
       register_bank_viewer_1_b_address_n1, register_bank_viewer_1_b_address_n2,
       register_bank_viewer_1_b_address_n3, register_bank_viewer_1_b_data_lsn,
       register_bank_viewer_1_b_data_msn, register_bank_viewer_1_c_address_n0,
       register_bank_viewer_1_c_address_n1, register_bank_viewer_1_c_address_n2,
       register_bank_viewer_1_c_address_n3, register_bank_viewer_1_c_data_lsn,
       register_bank_viewer_1_c_data_msn;
  wire [4:0] multiplexer_1_out;
  wire [5:0] A_Etapa1, ALU_Pipeline_a_bus_out, ALU_Pipeline_b_bus_out, ALU_Pipeline_t_bus_out, B_Etapa1,
       C_Etapa1, C_Etapa2Alu, C_Etapa2Mem, C_Etapa3, instruction2register_1_p3, instruction2register_1_p4,
       instruction2register_1_p5, judge_1_a_bus, judge_1_b_bus, judge_1_c_bus, LoadStore_a_bus_out,
       LoadStore_b_bus_out, pipeline_register_2_a_bus_out, pipeline_register_2_b_bus_out, T_after, Type_p,
       Type_prePip;
  wire [7:0] bloque1_bsr_1_p4, bloque1_bsr_1_p5, clk_edge_viewer_1_out_2, clk_edge_viewer_1_out_3,
       clk_edge_viewer_1_out_4, clk_edge_viewer_1_out_5, clk_edge_viewer_1_out_6, clk_edge_viewer_1_out_7,
       clk_edge_viewer_1_out_8, clk_edge_viewer_1_out_9, register_1_q_2, uc2_viewer_1_out_2,
       uc2_viewer_1_out_3, uc2_viewer_1_out_4, uc2_viewer_1_out_5, uc2_viewer_1_out_6, uc2_viewer_1_out_7,
       uc2_viewer_1_out_8, uc2_viewer_1_out_9, uc2_viewer_2_out_2, uc2_viewer_2_out_3, uc2_viewer_2_out_4,
       uc2_viewer_2_out_5, uc2_viewer_2_out_6, uc2_viewer_2_out_7, uc2_viewer_2_out_8, uc2_viewer_2_out_9;
  wire [8:8] ALU_Pipeline_kmx_out, pipeline_register_1_kmx_out;
  wire [9:0] ALU_Pipeline_d_address_out, instruction2register_1_p2, LoadStore_d_address_out,
       pipeline_register_1_d_address_out, register_4_q;
  wire [10:0] bloque1_bsr_1_p2, bloque1_bsr_1_p3;
  wire [14:0] judge_1_reg_out, LoadStore_t_bus_out, pipeline_register_2_t_bus_out;
  wire [14:6] MicroInstructionROM_microinstruction;
  wire [15:0] ALU_RESULT, ALUALULAU_z, bloque1_jmp_1_p4, BusA_ALU_q, BusA_LS_q, BusB_ALU_q, Constant_K_q,
       data_1_datamemout, dipswitch_1_sw16, dipswitch_2_sw16, instruction2register_1_p6, multiplexer_2_out,
       reg_C_write, register_1_q, register_7_q, register_bank_1_po0, register_bank_1_po1,
       register_bank_1_register_out_b_data, shiftersh_1_out_3;
  wire [23:0] BBUS, ProgramMemory_data;

  Hex_Digit_Display hex_digit_display_1 (.value({1'b0, bloque1_bsr_1_p4_2}));  // open: dp
  // Probe on {bloque1_bsr_1_p4_2, bloque1_bsr_1_p4}
  ROM #(.addrWidth(11), .dataWidth(24)) ProgramMemory (
    .addr({bloque1_bsr_1_p4_2, bloque1_bsr_1_p4}), .data(ProgramMemory_data));
  Clock sysclk ();  // open: out
  Hex_Digit_Display hex_digit_display_2 (.value(bloque1_bsr_1_p4[3:0]));  // open: dp
  Hex_Digit_Display hex_digit_display_3 (.value(bloque1_bsr_1_p4[7:4]));  // open: dp
  // Bloque1_bsr bloque1_bsr_1: pin names not known; wires that end beside it: CLK, bloque1_bsr_1_p2, bloque1_bsr_1_p3, {bloque1_bsr_1_p4_2, bloque1_bsr_1_p4}, bloque1_bsr_1_p5, bloque1_bsr_1_p6
  // Probe on HOLD
  // Probe on UC1_HOLD
  // Probe on CLK
  // Probe on undriven
  // Probe on undriven_2
  // Probe on undriven_3
  // Probe on undriven_4[1]
  // Probe on undriven_4[0]
  // Probe on undriven_5
  or or_1 (or_1_out, and_1_out, bloque1_bsr_1_p6);
  ClockGenerator clocks (.Auto(1'b1), .ManualCLK(in_1), .CLK(CLK), .CLK2(CLK2), .CLK3(CLK3), .CLK4(CLK4));
  // Probe on ProgramMemory_data
  // Bloque1_jmp bloque1_jmp_1: pin names not known; wires that end beside it: bloque1_bsr_1_p2, bloque1_bsr_1_p3, CYin, bloque1_jmp_1_p4, bloque1_bsr_1_p5, HOLD, bloque1_jmp_1_p4, CYin
  buf and_1 (and_1_out, ~HOLD);  // AND_Gate AND_Gate
  and and_2 (and_2_out, or_1_out, preloadenablee);
  or or_2 (or_2_out, HOLD, UC1_HOLD);
  Register #(.width(24), .trigger("falling")) register_1 (
    .D(BBUS), .en(not_1_out), .clk(CLK), .Q({register_1_q_2, register_1_q}));  // open: clr
  not not_1 (not_1_out, or_3_out);
  Register #(.width(24)) InstructionRegister (
    .D(ProgramMemory_data), .en(not_2_out), .clk(CLK), .Q(BBUS), .clr(undriven_6));
  not not_2 (not_2_out, HOLD);
  and and_3 (and_3_out, tvvv, Pr);
  not not_3 (not_3_out, T);
  // Probe on bloque1_bsr_1_p3
  Multiplexer #(.width(24), .enable("false")) multiplexer_1 (
    .in0({register_1_q_2, register_1_q}), .in1(BBUS),
    .out({bloque1_bsr_1_p5, bloque1_bsr_1_p2, multiplexer_1_out}), .sel(not_3_out));
  // jumpCont jumpcont_1: pin names not known; wires that end beside it: Type_p, T_after, Pr, jumpcont_1_p4, jumpcont_1_p4, T, tvvv, preloadenablee
  // Probe on {bloque1_bsr_1_p5, bloque1_bsr_1_p2, multiplexer_1_out}
  // Bloque1_jmp bloque1_jmp_2: pin names not known; wires that end beside it: register_1_q_2, Pr
  PCreg ProgramCounterReg (
    .PC({bloque1_bsr_1_p4_2, bloque1_bsr_1_p4}), .displacement_or_address(bloque1_bsr_1_p3), .HOLD(or_2_out),
    .CLK1(CLK), .Preload(and_2_out));
  // Probe on BBUS
  Hex_Digit_Display hex_digit_display_4 (.value(register_bank_viewer_1_c_data_msn));  // open: dp
  Hex_Digit_Display hex_digit_display_5 (.value(register_bank_viewer_1_c_data_lsn));  // open: dp
  DipSwitch #(.number(16)) dipswitch_1 (
    .sw1(dipswitch_1_sw16[15]), .sw2(dipswitch_1_sw16[14]), .sw3(dipswitch_1_sw16[13]),
    .sw4(dipswitch_1_sw16[12]), .sw5(dipswitch_1_sw16[11]), .sw6(dipswitch_1_sw16[10]),
    .sw7(dipswitch_1_sw16[9]), .sw8(dipswitch_1_sw16[8]), .sw9(dipswitch_1_sw16[7]),
    .sw10(dipswitch_1_sw16[6]), .sw11(dipswitch_1_sw16[5]), .sw12(dipswitch_1_sw16[4]),
    .sw13(dipswitch_1_sw16[3]), .sw14(dipswitch_1_sw16[2]), .sw15(dipswitch_1_sw16[1]),
    .sw16(dipswitch_1_sw16[0]));
  or or_3 (or_3_out, HOLD, UC1_HOLD);
  LED led_1 (.in(register_bank_viewer_1_c_is_enabled));
  Hex_Digit_Display hex_digit_display_6 (.value(register_bank_viewer_1_c_address_n3));  // open: dp
  Hex_Digit_Display hex_digit_display_7 (.value(register_bank_viewer_1_c_address_n2));  // open: dp
  DotMatrix #(.matrixcols(32), .matrixrows(32)) dotmatrix_1 ();  // open: col0, col1, col2, col3, col4, col5, col6, col7, col8, col9, col10, col11, col12, col13, col14, col15, col16, col17, col18, col19, col20, col21, col22, col23, col24, col25, col26, col27, col28, col29, col30, col31
  UC2_viewer uc2_viewer_1 (
    .out_6(uc2_viewer_1_out_6), .out_9(uc2_viewer_1_out_9), .out_7(uc2_viewer_1_out_7), .hold(UC1_HOLD),
    .out_4(uc2_viewer_1_out_4), .out_8(uc2_viewer_1_out_8), .out_5(uc2_viewer_1_out_5),
    .out_3(uc2_viewer_1_out_3), .out_2(uc2_viewer_1_out_2));
  DotMatrix #(.matrixcols(8), .matrixrows(8)) dotmatrix_2 (
    .col0(uc2_viewer_1_out_2), .col1(uc2_viewer_1_out_3), .col2(uc2_viewer_1_out_4),
    .col3(uc2_viewer_1_out_5), .col4(uc2_viewer_1_out_6), .col5(uc2_viewer_1_out_7),
    .col6(uc2_viewer_1_out_8), .col7(uc2_viewer_1_out_9));
  Hex_Digit_Display hex_digit_display_8 (.value(register_bank_viewer_1_c_address_n1));  // open: dp
  Hex_Digit_Display hex_digit_display_9 (.value(register_bank_viewer_1_c_address_n0));  // open: dp
  DipSwitch #(.number(16)) dipswitch_2 (
    .sw1(dipswitch_2_sw16[15]), .sw2(dipswitch_2_sw16[14]), .sw3(dipswitch_2_sw16[13]),
    .sw4(dipswitch_2_sw16[12]), .sw5(dipswitch_2_sw16[11]), .sw6(dipswitch_2_sw16[10]),
    .sw7(dipswitch_2_sw16[9]), .sw8(dipswitch_2_sw16[8]), .sw9(dipswitch_2_sw16[7]),
    .sw10(dipswitch_2_sw16[6]), .sw11(dipswitch_2_sw16[5]), .sw12(dipswitch_2_sw16[4]),
    .sw13(dipswitch_2_sw16[3]), .sw14(dipswitch_2_sw16[2]), .sw15(dipswitch_2_sw16[1]),
    .sw16(dipswitch_2_sw16[0]));
  Hex_Digit_Display hex_digit_display_10 (.value(register_bank_viewer_1_a_data_msn));  // open: dp
  Hex_Digit_Display hex_digit_display_11 ();  // open: value, dp
  // output_ports_viewer output_ports_viewer_1: pin names not known
  clk_edge_viewer clk_edge_viewer_1 (
    .out_6(clk_edge_viewer_1_out_6), .out_2(clk_edge_viewer_1_out_2), .out_9(clk_edge_viewer_1_out_9),
    .out_3(clk_edge_viewer_1_out_3), .out_7(clk_edge_viewer_1_out_7), .out_5(clk_edge_viewer_1_out_5),
    .in_1(CLK2), .out_8(clk_edge_viewer_1_out_8), .out_4(clk_edge_viewer_1_out_4));
  DotMatrix #(.matrixcols(8), .matrixrows(8)) dotmatrix_3 (
    .col0(clk_edge_viewer_1_out_2), .col1(clk_edge_viewer_1_out_3), .col2(clk_edge_viewer_1_out_4),
    .col3(clk_edge_viewer_1_out_5), .col4(clk_edge_viewer_1_out_6), .col5(clk_edge_viewer_1_out_7),
    .col6(clk_edge_viewer_1_out_8), .col7(clk_edge_viewer_1_out_9));
  // instruction2register instruction2register_1: pin names not known; wires that end beside it: BBUS, instruction2register_1_p2, instruction2register_1_p3, instruction2register_1_p4, instruction2register_1_p5, instruction2register_1_p6
  Hex_Digit_Display hex_digit_display_12 (.value(register_bank_viewer_1_a_data_lsn));  // open: dp
  Hex_Digit_Display hex_digit_display_13 (.value(register_bank_viewer_1_a_address_n3));  // open: dp
  Hex_Digit_Display hex_digit_display_14 ();  // open: value, dp
  Hex_Digit_Display hex_digit_display_15 ();  // open: value, dp
  Micro_Instruction_ROM MicroInstructionROM (
    .Instruction(BBUS), .MicroInstruction({MicroInstructionROM_microinstruction, Type_p}));
  LED led_2 (.in(register_bank_viewer_1_a_is_enabled));
  register_bank_viewer register_bank_viewer_1 (
    .A_data_LSN(register_bank_viewer_1_a_data_lsn), .C_data_MSN(register_bank_viewer_1_c_data_msn),
    .A_is_enabled(register_bank_viewer_1_a_is_enabled), .C_data_out(C_Etapa3),
    .A_address_N2(register_bank_viewer_1_a_address_n2), .C_address_N3(register_bank_viewer_1_c_address_n3),
    .B_is_enabled(register_bank_viewer_1_b_is_enabled), .A_address(bloque1_jmp_1_p4),
    .A_address_N1(register_bank_viewer_1_a_address_n1), .C_address_N2(register_bank_viewer_1_c_address_n2),
    .B_address_N3(register_bank_viewer_1_b_address_n3), .C_address_N0(register_bank_viewer_1_c_address_n0),
    .A_data_MSN(register_bank_viewer_1_a_data_msn), .C_address_N1(register_bank_viewer_1_c_address_n1),
    .A_address_N3(register_bank_viewer_1_a_address_n3), .C_address(reg_C_write), .A_data_out(A_Etapa1),
    .B_address_N1(register_bank_viewer_1_b_address_n1), .A_address_N0(register_bank_viewer_1_a_address_n0),
    .B_data_MSN(register_bank_viewer_1_b_data_msn), .B_address(register_bank_1_register_out_b_data),
    .C_data_LSN(register_bank_viewer_1_c_data_lsn), .B_data_LSN(register_bank_viewer_1_b_data_lsn),
    .B_address_N0(register_bank_viewer_1_b_address_n0), .B_data_out(B_Etapa1),
    .B_address_N2(register_bank_viewer_1_b_address_n2), .C_is_enabled(register_bank_viewer_1_c_is_enabled));
  Hex_Digit_Display hex_digit_display_16 (.value(register_bank_viewer_1_a_address_n1));  // open: dp
  Hex_Digit_Display hex_digit_display_17 (.value(register_bank_viewer_1_a_address_n2));  // open: dp
  DotMatrix #(.matrixcols(32), .matrixrows(32)) dotmatrix_4 ();  // open: col0, col1, col2, col3, col4, col5, col6, col7, col8, col9, col10, col11, col12, col13, col14, col15, col16, col17, col18, col19, col20, col21, col22, col23, col24, col25, col26, col27, col28, col29, col30, col31
  Hex_Digit_Display hex_digit_display_18 ();  // open: value, dp
  DotMatrix #(.matrixcols(17), .matrixrows(4)) dotmatrix_5 (
    .col0(pipeline_register_viewer_1_b16), .col1(pipeline_register_viewer_1_b15),
    .col2(pipeline_register_viewer_1_b14), .col3(pipeline_register_viewer_1_b13),
    .col4(pipeline_register_viewer_1_b12), .col5(pipeline_register_viewer_1_b11),
    .col6(pipeline_register_viewer_1_b10), .col7(pipeline_register_viewer_1_b9),
    .col8(pipeline_register_viewer_1_b8), .col9(pipeline_register_viewer_1_b7),
    .col10(pipeline_register_viewer_1_b6), .col11(pipeline_register_viewer_1_b5),
    .col12(pipeline_register_viewer_1_b4), .col13(pipeline_register_viewer_1_b3),
    .col14(pipeline_register_viewer_1_b2), .col15(pipeline_register_viewer_1_b1),
    .col16(pipeline_register_viewer_1_b0));
  pipeline_register_viewer pipeline_register_viewer_1 (
    .b9(pipeline_register_viewer_1_b9), .b16(pipeline_register_viewer_1_b16),
    .B_is_enabled(pipeline_register_viewer_1_b_is_enabled), .C_in(C_Etapa1),
    .b14(pipeline_register_viewer_1_b14), .b1(pipeline_register_viewer_1_b1),
    .b8(pipeline_register_viewer_1_b8), .A_in(A_Etapa1), .A_LSN(pipeline_register_viewer_1_a_lsn),
    .b6(pipeline_register_viewer_1_b6), .b7(pipeline_register_viewer_1_b7),
    .b0(pipeline_register_viewer_1_b0), .b11(pipeline_register_viewer_1_b11), .B_in(B_Etapa1),
    .B_MSN(pipeline_register_viewer_1_b_msn), .b15(pipeline_register_viewer_1_b15),
    .b4(pipeline_register_viewer_1_b4), .b3(pipeline_register_viewer_1_b3),
    .b10(pipeline_register_viewer_1_b10), .A_is_enabled(pipeline_register_viewer_1_a_is_enabled),
    .A_MSN(pipeline_register_viewer_1_a_msn), .b12(pipeline_register_viewer_1_b12),
    .b5(pipeline_register_viewer_1_b5), .b2(pipeline_register_viewer_1_b2),
    .b13(pipeline_register_viewer_1_b13),
    .microinstruction({pipeline_register_1_aluc_out, pipeline_register_1_sh_out, pipeline_register_1_kmx_out[8], pipeline_register_1_mrymw_out, T_after}),
    .B_LSN(pipeline_register_viewer_1_b_lsn), .C_is_enabled(pipeline_register_viewer_1_c_is_enabled),
    .C_MSN(pipeline_register_viewer_1_c_msn), .C_LSN(pipeline_register_viewer_1_c_lsn));
  // Probe on MicroInstructionROM_microinstruction[14:11]
  // Probe on MicroInstructionROM_microinstruction[10:9]
  // Probe on MicroInstructionROM_microinstruction[8]
  // Probe on MicroInstructionROM_microinstruction[7]
  // Probe on MicroInstructionROM_microinstruction[6]
  // Probe on Type_p
  Hex_Digit_Display hex_digit_display_19 (.value(register_bank_viewer_1_a_address_n0));  // open: dp
  Hex_Digit_Display hex_digit_display_20 ();  // open: value, dp
  Hex_Digit_Display hex_digit_display_21 (.value(register_bank_viewer_1_b_data_msn));  // open: dp
  Hex_Digit_Display hex_digit_display_22 ();  // open: value, dp
  Hex_Digit_Display hex_digit_display_23 ();  // open: value, dp
  Hex_Digit_Display hex_digit_display_24 (.value(register_bank_viewer_1_b_data_lsn));  // open: dp
  Hex_Digit_Display hex_digit_display_25 (.value(register_bank_viewer_1_b_address_n3));  // open: dp
  Hex_Digit_Display hex_digit_display_26 ();  // open: value, dp
  Hex_Digit_Display hex_digit_display_27 (.value(pipeline_register_viewer_1_c_msn));  // open: dp
  not not_4 (not_4_out, MEM_is_done);
  LED led_3 (.in(register_bank_viewer_1_b_is_enabled));
  Hex_Digit_Display hex_digit_display_28 (.value(register_bank_viewer_1_b_address_n2));  // open: dp
  Hex_Digit_Display hex_digit_display_29 (.value(register_bank_viewer_1_b_address_n1));  // open: dp
  LED led_4 (.in(pipeline_register_viewer_1_c_is_enabled));
  Hex_Digit_Display hex_digit_display_30 (.value(pipeline_register_viewer_1_c_lsn));  // open: dp
  // Probe on pipeline_register_1_aluc_out
  Pipeline_register pipeline_register_1 (
    .ALUC_OUT(pipeline_register_1_aluc_out), .B_bus_IN(instruction2register_1_p4),
    .SH_IN(MicroInstructionROM_microinstruction[10:9]), .D_Address_OUT(pipeline_register_1_d_address_out),
    .C_bus_OUT(C_Etapa1), .A_bus_OUT(A_Etapa1), .ALUC_IN(MicroInstructionROM_microinstruction[14:11]),
    .A_bus_IN(instruction2register_1_p3), .D_Address_IN(instruction2register_1_p2),
    .MRyMW_OUT(pipeline_register_1_mrymw_out), .SH_OUT(pipeline_register_1_sh_out),
    .C_bus_IN(instruction2register_1_p5), .Kmx_IN(MicroInstructionROM_microinstruction[8]), .Hold(or_3_out),
    .B_bus_OUT(B_Etapa1), .T_bus_OUT(T_after), .CLK(CLK2),
    .MRyMW_IN(MicroInstructionROM_microinstruction[7:6]), .T_bus_IN(Type_p),
    .Kmx_OUT(pipeline_register_1_kmx_out[8]));
  Hex_Digit_Display hex_digit_display_31 (.value(register_bank_viewer_1_b_address_n0));  // open: dp
  LED led_5 (.in(pipeline_register_viewer_1_a_is_enabled));
  Hex_Digit_Display hex_digit_display_32 (.value(pipeline_register_viewer_1_a_lsn));  // open: dp
  Hex_Digit_Display hex_digit_display_33 (.value(pipeline_register_viewer_1_a_msn));  // open: dp
  // Probe on A_Etapa1
  // Probe on B_Etapa1
  // Probe on C_Etapa1
  register_bank register_bank_1 (
    .clk(CLK), .register_out_A_address(A_Etapa1), .register_out_A_data(bloque1_jmp_1_p4),
    .register_in_address(C_Etapa3), .register_in_data(reg_C_write), .register_out_B_address(B_Etapa1),
    .register_out_B_data(register_bank_1_register_out_b_data), .PI0(dipswitch_1_sw16),
    .PI1(dipswitch_2_sw16), .PO0(register_bank_1_po0), .PO1(register_bank_1_po1));  // open: register_out_aux_address, register_out_aux_data
  LED led_6 (.in(pipeline_register_viewer_1_b_is_enabled));
  Hex_Digit_Display hex_digit_display_34 (.value(pipeline_register_viewer_1_b_lsn));  // open: dp
  Hex_Digit_Display hex_digit_display_35 (.value(pipeline_register_viewer_1_b_msn));  // open: dp
  // Probe on T_after
  // Probe on nothing
  // Probe on C_Etapa3
  // UC1 uc1_1: pin names not known; wires that end beside it: HOLD, pipeline_register_1_mrymw_out, not_4_out, mem_is_free, uc1_1_p5, uc1_1_p6, LatchMemEnable, UC1_HOLD
  not not_5 (not_5_out, HOLD);
  // Probe on nothing
  Register #(.width(1)) register_2 (.D(uc1_1_p5), .clk(CLK2), .Q(register_2_q));  // open: en, clr
  Register #(.width(16), .trigger("falling")) Constant_K (
    .D(instruction2register_1_p6), .en(not_5_out), .clk(CLK2), .Q(Constant_K_q));  // open: clr
  Register #(.width(1), .trigger("falling")) register_3 (.D(uc1_1_p6), .clk(CLK2), .Q(register_3_q));  // open: en, clr
  not not_6 (not_6_out, pipeline_register_1_kmx_out[8]);
  Register #(.width(16)) BusA_ALU (.D(multiplexer_2_out), .en(uc1_1_p5), .clk(CLK2), .Q(BusA_ALU_q));  // open: clr
  Multiplexer #(.width(16), .enable("false")) multiplexer_2 (
    .in0(Constant_K_q), .in1(bloque1_jmp_1_p4), .out(multiplexer_2_out), .sel(not_6_out));
  Register #(.width(16)) BusB_ALU (
    .D(register_bank_1_register_out_b_data), .en(uc1_1_p5), .clk(CLK2), .Q(BusB_ALU_q));  // open: clr
  Register #(.width(10), .trigger("falling")) register_4 (
    .D(pipeline_register_1_d_address_out), .en(uc1_1_p6), .clk(CLK2), .Q(register_4_q));  // open: clr
  DotMatrix #(.matrixcols(17), .matrixrows(4)) dotmatrix_6 (
    .col0(pipeline_register_viewer_2_b16), .col1(pipeline_register_viewer_2_b15),
    .col2(pipeline_register_viewer_2_b14), .col3(pipeline_register_viewer_2_b13),
    .col4(pipeline_register_viewer_2_b12), .col5(pipeline_register_viewer_2_b11),
    .col6(pipeline_register_viewer_2_b10), .col7(pipeline_register_viewer_2_b9),
    .col8(pipeline_register_viewer_2_b8), .col9(pipeline_register_viewer_2_b7),
    .col10(pipeline_register_viewer_2_b6), .col11(pipeline_register_viewer_2_b5),
    .col12(pipeline_register_viewer_2_b4), .col13(pipeline_register_viewer_2_b3),
    .col14(pipeline_register_viewer_2_b2), .col15(pipeline_register_viewer_2_b1),
    .col16(pipeline_register_viewer_2_b0));
  pipeline_register_viewer pipeline_register_viewer_2 (
    .b9(pipeline_register_viewer_2_b9), .b16(pipeline_register_viewer_2_b16),
    .B_is_enabled(pipeline_register_viewer_2_b_is_enabled), .C_in(C_Etapa2Alu),
    .b14(pipeline_register_viewer_2_b14), .b1(pipeline_register_viewer_2_b1),
    .b8(pipeline_register_viewer_2_b8), .A_in(ALU_Pipeline_a_bus_out),
    .A_LSN(pipeline_register_viewer_2_a_lsn), .b6(pipeline_register_viewer_2_b6),
    .b7(pipeline_register_viewer_2_b7), .b0(pipeline_register_viewer_2_b0),
    .b11(pipeline_register_viewer_2_b11), .B_in(ALU_Pipeline_b_bus_out),
    .B_MSN(pipeline_register_viewer_2_b_msn), .b15(pipeline_register_viewer_2_b15),
    .b4(pipeline_register_viewer_2_b4), .b3(pipeline_register_viewer_2_b3),
    .b10(pipeline_register_viewer_2_b10), .A_is_enabled(pipeline_register_viewer_2_a_is_enabled),
    .A_MSN(pipeline_register_viewer_2_a_msn), .b12(pipeline_register_viewer_2_b12),
    .b5(pipeline_register_viewer_2_b5), .b2(pipeline_register_viewer_2_b2),
    .b13(pipeline_register_viewer_2_b13),
    .microinstruction({ALU_Pipeline_aluc_out, ALU_Pipeline_sh_out, ALU_Pipeline_kmx_out[8], MREtapa2Pipeline, ALU_Pipeline_t_bus_out}),
    .B_LSN(pipeline_register_viewer_2_b_lsn), .C_is_enabled(pipeline_register_viewer_2_c_is_enabled),
    .C_MSN(pipeline_register_viewer_2_c_msn), .C_LSN(pipeline_register_viewer_2_c_lsn));
  not not_7 (not_7_out, uc1_1_p5);
  and and_4 (and_4_out, ~CLK3, register_3_q);  // AND_Gate
  Register #(.width(16), .trigger("falling")) BusA_LS (
    .D(bloque1_jmp_1_p4), .en(uc1_1_p6), .clk(CLK2), .Q(BusA_LS_q));  // open: clr
  // Probe on BusA_ALU_q
  // Probe on BusB_ALU_q
  DotMatrix #(.matrixcols(17), .matrixrows(4)) dotmatrix_7 (
    .col0(pipeline_register_viewer_3_b16), .col1(pipeline_register_viewer_3_b15),
    .col2(pipeline_register_viewer_3_b14), .col3(pipeline_register_viewer_3_b13),
    .col4(pipeline_register_viewer_3_b12), .col5(pipeline_register_viewer_3_b11),
    .col6(pipeline_register_viewer_3_b10), .col7(pipeline_register_viewer_3_b9),
    .col8(pipeline_register_viewer_3_b8), .col9(pipeline_register_viewer_3_b7),
    .col10(pipeline_register_viewer_3_b6), .col11(pipeline_register_viewer_3_b5),
    .col12(pipeline_register_viewer_3_b4), .col13(pipeline_register_viewer_3_b3),
    .col14(pipeline_register_viewer_3_b2), .col15(pipeline_register_viewer_3_b1),
    .col16(pipeline_register_viewer_3_b0));
  pipeline_register_viewer pipeline_register_viewer_3 (
    .b9(pipeline_register_viewer_3_b9), .b16(pipeline_register_viewer_3_b16),
    .B_is_enabled(pipeline_register_viewer_3_b_is_enabled), .C_in(C_Etapa2Mem),
    .b14(pipeline_register_viewer_3_b14), .b1(pipeline_register_viewer_3_b1),
    .b8(pipeline_register_viewer_3_b8), .A_in(LoadStore_a_bus_out), .A_LSN(pipeline_register_viewer_3_a_lsn),
    .b6(pipeline_register_viewer_3_b6), .b7(pipeline_register_viewer_3_b7),
    .b0(pipeline_register_viewer_3_b0), .b11(pipeline_register_viewer_3_b11), .B_in(LoadStore_b_bus_out),
    .B_MSN(pipeline_register_viewer_3_b_msn), .b15(pipeline_register_viewer_3_b15),
    .b4(pipeline_register_viewer_3_b4), .b3(pipeline_register_viewer_3_b3),
    .b10(pipeline_register_viewer_3_b10), .A_is_enabled(pipeline_register_viewer_3_a_is_enabled),
    .A_MSN(pipeline_register_viewer_3_a_msn), .b12(pipeline_register_viewer_3_b12),
    .b5(pipeline_register_viewer_3_b5), .b2(pipeline_register_viewer_3_b2),
    .b13(pipeline_register_viewer_3_b13),
    .microinstruction({LoadStore_t_bus_out[14:8], MRMW, LoadStore_t_bus_out[5:0]}),
    .B_LSN(pipeline_register_viewer_3_b_lsn), .C_is_enabled(pipeline_register_viewer_3_c_is_enabled),
    .C_MSN(pipeline_register_viewer_3_c_msn), .C_LSN(pipeline_register_viewer_3_c_lsn));
  not not_8 (not_8_out, uc1_1_p6);
  Register #(.width(1)) register_5 (.D(ALUALULAU_cyout), .en(1'b1), .clk(CLK2), .Q(CYin));  // open: clr
  LED led_7 (.in(pipeline_register_viewer_2_c_is_enabled));
  Hex_Digit_Display hex_digit_display_36 (.value(pipeline_register_viewer_2_c_msn));  // open: dp
  or or_4 (or_4_out, mem_is_free, nor_1_out);
  nor nor_1 (nor_1_out, mem_is_free, MEM_is_done);
  and and_5 (and_5_out, register_2_q, CLK3);
  ALU ALUALULAU (
    .ALUC(ALU_Pipeline_aluc_out), .A(BusA_ALU_q), .B(BusB_ALU_q), .CYin(CYin), .Z(ALUALULAU_z),
    .CYout(ALUALULAU_cyout));
  LED led_8 (.in(pipeline_register_viewer_2_a_is_enabled));
  Hex_Digit_Display hex_digit_display_37 (.value(pipeline_register_viewer_2_c_lsn));  // open: dp
  Hex_Digit_Display hex_digit_display_38 (.value(pipeline_register_viewer_2_a_msn));  // open: dp
  Pipeline_register ALU_Pipeline (
    .ALUC_OUT(ALU_Pipeline_aluc_out), .B_bus_IN(B_Etapa1), .SH_IN(pipeline_register_1_sh_out),
    .D_Address_OUT(ALU_Pipeline_d_address_out), .C_bus_OUT(C_Etapa2Alu), .A_bus_OUT(ALU_Pipeline_a_bus_out),
    .ALUC_IN(pipeline_register_1_aluc_out), .A_bus_IN(A_Etapa1),
    .D_Address_IN(pipeline_register_1_d_address_out), .MRyMW_OUT(MREtapa2Pipeline),
    .SH_OUT(ALU_Pipeline_sh_out), .C_bus_IN(C_Etapa1), .Kmx_IN(pipeline_register_1_kmx_out[8]),
    .Hold(not_7_out), .B_bus_OUT(ALU_Pipeline_b_bus_out), .T_bus_OUT(ALU_Pipeline_t_bus_out), .CLK(CLK3),
    .MRyMW_IN(pipeline_register_1_mrymw_out), .T_bus_IN(T_after), .Kmx_OUT(ALU_Pipeline_kmx_out[8]));
  and and_6 (and_6_out, ~uc1_1_p5, or_4_out);  // AND_Gate
  // Probe on ALUALULAU_z
  LED led_9 (.in(pipeline_register_viewer_3_c_is_enabled));
  Hex_Digit_Display hex_digit_display_39 (.value(pipeline_register_viewer_3_c_lsn));  // open: dp
  Hex_Digit_Display hex_digit_display_40 (.value(pipeline_register_viewer_3_c_msn));  // open: dp
  Pipeline_register LoadStore (
    .ALUC_OUT(LoadStore_t_bus_out[14:11]), .B_bus_IN(B_Etapa1), .SH_IN(pipeline_register_1_sh_out),
    .D_Address_OUT(LoadStore_d_address_out), .C_bus_OUT(C_Etapa2Mem), .A_bus_OUT(LoadStore_a_bus_out),
    .ALUC_IN(pipeline_register_1_aluc_out), .A_bus_IN(A_Etapa1),
    .D_Address_IN(pipeline_register_1_d_address_out), .MRyMW_OUT(MRMW), .SH_OUT(LoadStore_t_bus_out[10:9]),
    .C_bus_IN(C_Etapa1), .Kmx_IN(pipeline_register_1_kmx_out[8]), .Hold(not_8_out),
    .B_bus_OUT(LoadStore_b_bus_out), .T_bus_OUT(LoadStore_t_bus_out[5:0]), .CLK(CLK3),
    .MRyMW_IN(pipeline_register_1_mrymw_out), .T_bus_IN(T_after), .Kmx_OUT(LoadStore_t_bus_out[8]));
  and and_7 (and_7_out, MEM_is_done, ~mem_is_free);  // AND_Gate
  Hex_Digit_Display hex_digit_display_41 (.value(pipeline_register_viewer_2_a_lsn));  // open: dp
  Hex_Digit_Display hex_digit_display_42 (.value(pipeline_register_viewer_2_b_msn));  // open: dp
  LED led_10 (.in(pipeline_register_viewer_3_a_is_enabled));
  Hex_Digit_Display hex_digit_display_43 (.value(pipeline_register_viewer_3_a_msn));  // open: dp
  Hex_Digit_Display hex_digit_display_44 (.value(pipeline_register_viewer_3_a_lsn));  // open: dp
  Data data_1 (
    .DAddress(register_4_q), .M(MRMW), .clk(CLK2), .Enable(register_3_q), .DataMemInput(BusA_LS_q),
    .DataMemOut(data_1_datamemout));
  LED led_11 (.in(pipeline_register_viewer_2_b_is_enabled));
  Hex_Digit_Display hex_digit_display_45 (.value(pipeline_register_viewer_2_b_lsn));  // open: dp
  Register #(.width(16)) register_6 (.D(shiftersh_1_out_3), .en(1'b1), .clk(CLK2), .Q(ALU_RESULT));  // open: clr
  // Probe on shiftersh_1_out_3
  ShifterSH shiftersh_1 (.ShifterIn(ALUALULAU_z), .SH(ALU_Pipeline_sh_out), .out_3(shiftersh_1_out_3));
  LED led_12 (.in(pipeline_register_viewer_3_b_is_enabled));
  Hex_Digit_Display hex_digit_display_46 (.value(pipeline_register_viewer_3_b_msn));  // open: dp
  // Probe on MRMW
  // Probe on LoadStore_d_address_out
  // Probe on data_1_datamemout
  ALU_unit_control alu_unit_control_1 (
    .set_free(and_6_out), .set_not_free(and_5_out), .clk(CLK3), .is_free(ALU_is_free), .is_done(ALU_is_done));
  Hex_Digit_Display hex_digit_display_47 (.value(pipeline_register_viewer_3_b_lsn));  // open: dp
  // Probe on mem_is_free
  memory_unit_control memory_unit_control_1 (
    .set_free(and_7_out), .set_not_free(and_4_out), .clk(CLK2), .is_free(mem_is_free), .is_done(MEM_is_done));
  Register #(.width(16)) register_7 (.D(data_1_datamemout), .en(1'b1), .clk(CLK2), .Q(register_7_q));  // open: clr
  DotMatrix #(.inputtype("row"), .matrixcols(16), .matrixrows(16)) dotmatrix_8 ();  // open: row0, row1, row2, row3, row4, row5, row6, row7, row8, row9, row10, row11, row12, row13, row14, row15
  // stage2_status_viewer stage2_status_viewer_1: pin names not known; wires that end beside it: ALU_is_free, ALU_is_done
  DotMatrix #(.inputtype("row"), .matrixcols(16), .matrixrows(16)) dotmatrix_9 ();  // open: row0, row1, row2, row3, row4, row5, row6, row7, row8, row9, row10, row11, row12, row13, row14, row15
  DotMatrix #(.inputtype("row"), .matrixcols(16), .matrixrows(16)) dotmatrix_10 ();  // open: row0, row1, row2, row3, row4, row5, row6, row7, row8, row9, row10, row11, row12, row13, row14, row15
  Multiplexer #(.width(16), .enable("false")) multiplexer_3 (
    .in0(ALU_RESULT), .in1(register_7_q), .out(reg_C_write), .sel(MEM_is_done));
  // stage2_status_viewer stage2_status_viewer_2: pin names not known; wires that end beside it: mem_is_free, MEM_is_done
  DotMatrix #(.inputtype("row"), .matrixcols(16), .matrixrows(16)) dotmatrix_11 ();  // open: row0, row1, row2, row3, row4, row5, row6, row7, row8, row9, row10, row11, row12, row13, row14, row15
  DotMatrix #(.inputtype("row"), .matrixcols(16), .matrixrows(16)) dotmatrix_12 ();  // open: row0, row1, row2, row3, row4, row5, row6, row7, row8, row9, row10, row11, row12, row13, row14, row15
  DotMatrix #(.inputtype("row"), .matrixcols(16), .matrixrows(16)) dotmatrix_13 ();  // open: row0, row1, row2, row3, row4, row5, row6, row7, row8, row9, row10, row11, row12, row13, row14, row15
  judge judge_1 (
    .reg_in_alu({ALU_Pipeline_aluc_out, ALU_Pipeline_sh_out, ALU_Pipeline_kmx_out[8], MREtapa2Pipeline, ALU_Pipeline_t_bus_out}),
    .reg_in_memory({LoadStore_t_bus_out[14:8], MRMW, LoadStore_t_bus_out[5:0]}),
    .A_alu(ALU_Pipeline_a_bus_out), .A_mem(LoadStore_a_bus_out), .B_alu(ALU_Pipeline_b_bus_out),
    .B_mem(LoadStore_b_bus_out), .C_alu(C_Etapa2Alu), .C_mem(C_Etapa2Mem), .in_9({MEM_is_done, ALU_is_done}),
    .reg_out(judge_1_reg_out), .A_bus(judge_1_a_bus), .B_bus(judge_1_b_bus), .C_bus(judge_1_c_bus));
  UC2_viewer uc2_viewer_2 (
    .out_6(uc2_viewer_2_out_6), .out_9(uc2_viewer_2_out_9), .out_7(uc2_viewer_2_out_7), .hold(HOLD),
    .out_4(uc2_viewer_2_out_4), .out_8(uc2_viewer_2_out_8), .out_5(uc2_viewer_2_out_5),
    .out_3(uc2_viewer_2_out_3), .out_2(uc2_viewer_2_out_2));
  DotMatrix #(.matrixcols(8), .matrixrows(8)) dotmatrix_14 (
    .col0(uc2_viewer_2_out_2), .col1(uc2_viewer_2_out_3), .col2(uc2_viewer_2_out_4),
    .col3(uc2_viewer_2_out_5), .col4(uc2_viewer_2_out_6), .col5(uc2_viewer_2_out_7),
    .col6(uc2_viewer_2_out_8), .col7(uc2_viewer_2_out_9));
  // UC2 uc2_1: pin names not known; wires that end beside it: A_Etapa1, B_Etapa1, C_Etapa1, C_Etapa2Alu, ALU_is_free, C_Etapa2Mem, mem_is_free, C_Etapa3, Type_prePip, CLK, HOLD
  pipeline_register_viewer pipeline_register_viewer_4 (
    .b9(pipeline_register_viewer_4_b9), .b16(pipeline_register_viewer_4_b16),
    .B_is_enabled(pipeline_register_viewer_4_b_is_enabled), .C_in(C_Etapa3),
    .b14(pipeline_register_viewer_4_b14), .b1(pipeline_register_viewer_4_b1),
    .b8(pipeline_register_viewer_4_b8), .A_in(pipeline_register_2_a_bus_out),
    .A_LSN(pipeline_register_viewer_4_a_lsn), .b6(pipeline_register_viewer_4_b6),
    .b7(pipeline_register_viewer_4_b7), .b0(pipeline_register_viewer_4_b0),
    .b11(pipeline_register_viewer_4_b11), .B_in(pipeline_register_2_b_bus_out),
    .B_MSN(pipeline_register_viewer_4_b_msn), .b15(pipeline_register_viewer_4_b15),
    .b4(pipeline_register_viewer_4_b4), .b3(pipeline_register_viewer_4_b3),
    .b10(pipeline_register_viewer_4_b10), .A_is_enabled(pipeline_register_viewer_4_a_is_enabled),
    .A_MSN(pipeline_register_viewer_4_a_msn), .b12(pipeline_register_viewer_4_b12),
    .b5(pipeline_register_viewer_4_b5), .b2(pipeline_register_viewer_4_b2),
    .b13(pipeline_register_viewer_4_b13), .microinstruction(pipeline_register_2_t_bus_out),
    .B_LSN(pipeline_register_viewer_4_b_lsn), .C_is_enabled(pipeline_register_viewer_4_c_is_enabled),
    .C_MSN(pipeline_register_viewer_4_c_msn), .C_LSN(pipeline_register_viewer_4_c_lsn));
  DotMatrix #(.matrixcols(17), .matrixrows(4)) dotmatrix_15 (
    .col0(pipeline_register_viewer_4_b16), .col1(pipeline_register_viewer_4_b15),
    .col2(pipeline_register_viewer_4_b14), .col3(pipeline_register_viewer_4_b13),
    .col4(pipeline_register_viewer_4_b12), .col5(pipeline_register_viewer_4_b11),
    .col6(pipeline_register_viewer_4_b10), .col7(pipeline_register_viewer_4_b9),
    .col8(pipeline_register_viewer_4_b8), .col9(pipeline_register_viewer_4_b7),
    .col10(pipeline_register_viewer_4_b6), .col11(pipeline_register_viewer_4_b5),
    .col12(pipeline_register_viewer_4_b4), .col13(pipeline_register_viewer_4_b3),
    .col14(pipeline_register_viewer_4_b2), .col15(pipeline_register_viewer_4_b1),
    .col16(pipeline_register_viewer_4_b0));
  LED led_13 (.in(pipeline_register_viewer_4_c_is_enabled));
  Hex_Digit_Display hex_digit_display_48 (.value(pipeline_register_viewer_4_c_msn));  // open: dp
  Hex_Digit_Display hex_digit_display_49 (.value(pipeline_register_viewer_4_c_lsn));  // open: dp
  Pipeline_register pipeline_register_2 (
    .ALUC_OUT(pipeline_register_2_t_bus_out[14:11]), .B_bus_IN(judge_1_b_bus), .SH_IN(judge_1_reg_out[10:9]),
    .C_bus_OUT(C_Etapa3), .A_bus_OUT(pipeline_register_2_a_bus_out), .ALUC_IN(judge_1_reg_out[14:11]),
    .A_bus_IN(judge_1_a_bus), .MRyMW_OUT(pipeline_register_2_t_bus_out[7:6]),
    .SH_OUT(pipeline_register_2_t_bus_out[10:9]), .C_bus_IN(judge_1_c_bus), .Kmx_IN(judge_1_reg_out[8]),
    .Hold(undriven_7), .B_bus_OUT(pipeline_register_2_b_bus_out),
    .T_bus_OUT(pipeline_register_2_t_bus_out[5:0]), .CLK(CLK3), .MRyMW_IN(judge_1_reg_out[7:6]),
    .T_bus_IN(judge_1_reg_out[5:0]), .Kmx_OUT(pipeline_register_2_t_bus_out[8]));  // open: D_Address_OUT, D_Address_IN
  LED led_14 (.in(pipeline_register_viewer_4_a_is_enabled));
  Hex_Digit_Display hex_digit_display_50 (.value(pipeline_register_viewer_4_a_lsn));  // open: dp
  Hex_Digit_Display hex_digit_display_51 (.value(pipeline_register_viewer_4_a_msn));  // open: dp
  LED led_15 (.in(pipeline_register_viewer_4_b_is_enabled));
  Hex_Digit_Display hex_digit_display_52 (.value(pipeline_register_viewer_4_b_lsn));  // open: dp
  Hex_Digit_Display hex_digit_display_53 (.value(pipeline_register_viewer_4_b_msn));  // open: dp
  or or_5 (or_5_out, 1'b1, 1'b1, 1'b1, 1'b1, 1'b1);
  or or_6 (or_6_out, 1'b1, 1'b1, 1'b1, 1'b1, 1'b1);
  or or_7 (or_7_out, 1'b1, 1'b1, 1'b1, 1'b1, 1'b1);
  and and_8 (and_8_out, or_5_out, 1'b1);
  and and_9 (and_9_out, or_6_out, 1'b1);
  and and_10 (and_10_out, ~or_7_out, 1'b1);  // AND_Gate
  or or_8 (or_8_out, and_8_out, and_9_out);
  // AND_Gate and_11 has open pins: in0=or_8_out, in1=and_10_out, out=open
  // NOT_Gate not_9 is placed but not wired

  // Other names for the same wires on the sheet: pulseGenManual = in_1; reg_C_address[5:0] = C_Etapa3

  // Notes on the sheet:
  //   contents of ProgramMemory (hex, n*v repeats v):
  //   1001e0 800034 800035 1000e0 ffffe0 7000e0 400060 a029e a02bf 400120 20000 852b6 a0295 a02d4 10000
  //   a0380 20000 e00020 700280 4001e0 a03a0 10000
  //   PC
  //   splitters que encajar con los registros de pipeline
  //   para hacer copy-paste
  //   probes que encajar en los splitters de arriba
  //   INSTRUCTION
  //   REGISTER
  //   Y USAR EL DISPLAY EN LOS PUERTOS DE SALIDA PO0 Y PO1
  //   LA IDEA ES USAR LOS DIP SWITCH EN LOS PUERTOS DE ENTRADA PI0 Y PI1
  //   ESTA CONEXION ES SOLO DE PRUEBA
  //   Detecto nueva operacion de memoria
  //   El mux es el de los is_done , el menos significativo es el de la ALU que se pone en 1 cuando termino
endmodule
