// Logisim project UC1.circ as structural Verilog: 1 circuit, main circuit UC1
module UC1 (
  input  HOLD,
  input  [1:0] MRyMW_OUT_E1,
  input  ALUisFree,
  input  MEMisFree,
  output ALUEnable,
  output LoadStoreEnable
);

  wire or_1_out;

  or or_1 (or_1_out, MRyMW_OUT_E1[0], MRyMW_OUT_E1[1]);
  and and_1 (ALUEnable, ~HOLD, ~or_1_out, ALUisFree);  // AND_Gate
  and and_2 (LoadStoreEnable, ~HOLD, or_1_out, MEMisFree);  // AND_Gate
endmodule
